# Fritzing sketch Circuit (saved by Fritzing 0.9.10b)
circuit board: 9cm x 12cm
perfboards: 2

parts:
  MAX31865_#3 = Adafruit MAX31865 RTD Sensor Breakout [part_number="Adafruit #3328"]
  MAX31865_#4 = Adafruit MAX31865 RTD Sensor Breakout [part_number="Adafruit #3328"]
  RTC = Adafruit DS3231 [part_number="Adafruit #3013"]
  MAX31865_#2 = Adafruit MAX31865 RTD Sensor Breakout [part_number="Adafruit #3328"]
  MAX31865_#1 = Adafruit MAX31865 RTD Sensor Breakout [part_number="Adafruit #3328"]
  Logger = Adafruit Feather M0 Adalogger [part_number="Adafruit #2796"]
  MAX31865_#5 = Adafruit MAX31865 RTD Sensor Breakout [part_number="Adafruit #3328"]
  DS18B20 = screw terminal, 3 pins
  R1 = Resistor [tolerance=±1% power=0.25 resistance=4.7k package=THT]

nets:
  VIN: MAX31865_#3.VIN, MAX31865_#4.VIN, RTC.Vin, MAX31865_#2.VIN, MAX31865_#1.VIN, Logger.+3V3, MAX31865_#5.VIN, DS18B20.pin1, R1.Pin_1
  GND: MAX31865_#3.GND, MAX31865_#4.GND, RTC.GND, MAX31865_#2.GND, MAX31865_#1.GND, Logger.GND, MAX31865_#5.GND, DS18B20.pin3
  N1: MAX31865_#3.SCLK, MAX31865_#4.SCLK, MAX31865_#2.SCLK, MAX31865_#1.SCLK, Logger.D13, MAX31865_#5.SCLK
  N2: MAX31865_#3.SDO, MAX31865_#4.SDO, MAX31865_#2.SDO, MAX31865_#1.SDO, Logger.D12, MAX31865_#5.SDO
  N3: MAX31865_#3.SDI, MAX31865_#4.SDI, MAX31865_#2.SDI, MAX31865_#1.SDI, Logger.D11, MAX31865_#5.SDI
  N4: MAX31865_#3.CS, Logger.D9
  N5: MAX31865_#4.CS, Logger.D6
  N6: RTC.SCL, Logger.SCL
  N7: RTC.SDA, Logger.SDA
  N8: RTC.SQW, Logger.D0
  N9: MAX31865_#2.CS, Logger.D1
  N10: MAX31865_#1.CS, Logger.D5
  N11: Logger.A0, DS18B20.pin2, R1.Pin_0
  N12: Logger.D10, MAX31865_#5.CS

notes:
  VIN
  GND
  3V3
  CLK
  SDO
  SDI
  CS
  RDY
  SCL
  SDA
  BAT
  32K
  SQW
  RST
  D5
  D6
  D9
  D10
  D11
  D12
  D13
  USB
  EN
  VBAT
  D1
  D0
  MISO
  MOSI
  SCK
  A5
  A4
  A3
  A2
  A1
  A0
  AREF
  3.3V
  RESET
  A0 - DATA
  4.7k
  DATA
  UNIL - ISTE
  RISK
  GROUP
  v1.0 - aug 2022

custom parts:
  Adafruit MAX31865 RTD Sensor Breakout: For precision temperature sensing, nothing beats a Platinum RTD. Resistance temperature detectors (RTDs) are temperature sensors that contain a resistor that changes resistance value as its temperature changes, basically a kind of thermistor. In this sensor, the resistor is actually a small strip of Platinum with a resistance of 100 ohms at 0°C, thus the name PT100. Compared to most NTC/PTC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
  Adafruit DS3231: The datasheet for the DS3231 explains that this part is an "Extremely Accurate I²C-Integrated RTC/TCXO/Crystal". And, hey, it does exactly what it says on the tin! This Real Time Clock (RTC) is the most precise you can get in a small, low power package. Most RTCs use an external 32kHz timing crystal that is used to keep time with low current draw. And that's all well and good, but those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
  Adafruit Feather M0 Adalogger: This is the Adafruit Feather M0 Adalogger - our take on an 'all-in-one' Cortex M0 datalogger (or data-reader) with built in USB and battery charging. Its an Adafruit Feather M0 with a microSD holder ready to rock! We have other boards in the Feather family, check'em out here At the Feather M0's heart is an ATSAMD21G18 ARM Cortex M0 processor, clocked at 48 MHz and at 3.3V logic, the same one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
